# Fritzing sketch schema_mc02_v8 (saved by Fritzing 0.8.5b)
breadboards: 6

parts:
  CNY74-1 = CNY74-4
  Part1 = Arduino Mega 2560 (Rev3)
  IR1 = TSOP312.., 314.. [package=THT]
  R1 = Resistor [tolerance=±5% resistance=4.7k package=THT]
  GY1 = MPU-6050 Board GY-521 [form="♀ (female)" package=THT]
  S2 = Round Pushbutton
  DS1 = DS18B20 1-Wire Temperature Sensor [part_number=DS18B20]
  U1 = 2-Channel 5v Relay Shield [package=relay-2ch5v10a]
  U2 = 2-Channel 5v Relay Shield [package=relay-2ch5v10a]
  U3 = 2-Channel 5v Relay Shield [package=relay-2ch5v10a]
  U4 = SWITCH_SPDT [package=kps-1290]
  M1 = DC Motor
  M2 = DC Motor
  Power_plug1 = Power plug
  S1 = Round Pushbutton
  F1 = FUSE [package=fuse_5mm]
  Power_plug2 = Power plug  # not connected
  Power_plug3 = Power plug  # not connected
  M3 = Stepper Motor - Unipolar
  DS2 = DS18B20 1-Wire Temperature Sensor [part_number=DS18B20]
  DS3 = DS18B20 1-Wire Temperature Sensor [part_number=DS18B20]
  DS4 = DS18B20 1-Wire Temperature Sensor [part_number=DS18B20]
  Part2 = Arduino Nano (Rev3.0)
  J1 = Piezo Speaker
  S3 = Round Pushbutton
  S4 = Round Pushbutton
  S5 = Round Pushbutton
  S6 = Round Pushbutton
  R2 = Resistor [tolerance=±5% resistance=1k package=THT]
  R3 = Resistor [tolerance=±5% resistance=1k package=THT]
  R4 = Resistor [tolerance=±5% resistance=1k package=THT]
  R5 = Resistor [tolerance=±5% resistance=1k package=THT]
  S7 = Round Pushbutton

nets:
  N1: CNY74-1.D1-A#0, R2.Pin_0
  N2: CNY74-1.D1-C, S4.leg1
  N3: CNY74-1.D2-C, S3.leg1
  N4: CNY74-1.D1-A#3, R3.Pin_0
  N5: CNY74-1.D3-A, R4.Pin_0
  N6: CNY74-1.D3-C, S5.leg1
  N7: CNY74-1.D4-C, S6.leg1
  N8: CNY74-1.D4-A, R5.Pin_0
  GND: CNY74-1.T4-E, CNY74-1.T3-E, CNY74-1.T2-E, CNY74-1.T1-E, Part1.GND, IR1.Vs, GY1.pin2, U2.GND, S3.leg0, S4.leg0, S7.leg0
  N9: CNY74-1.T4-C, Part1.D40
  N10: CNY74-1.T3-C, Part1.D42
  N11: CNY74-1.T2-C, Part1.D44
  N12: CNY74-1.T1-C, Part1.D38
  N13: Part1.D21/SCL, GY1.pin3
  N14: Part1.D20/SDA, GY1.pin4, GY1.pin5
  5V: Part1.5V, IR1.Data, GY1.pin1, U2.VCC, R2.Pin_1, R3.Pin_1, R4.Pin_1, R5.Pin_1
  N15: Part1.D5_PWM, IR1.GND
  N16: Part1.D53, U2.IN1, U2.IN2
  N17: R1.Pin_0, DS1.DQ, DS2.DQ, DS3.DQ, DS4.DQ, Part2.D2
  VDD: R1.Pin_1, DS1.VDD, DS2.VDD, DS3.VDD, DS4.VDD, Part2.5V
  N18: S2.leg0, S1.leg1
  N19: S2.leg1, U4.O
  GND_2: DS1.GND, DS2.GND, DS3.GND, DS4.GND, Part2.GND, J1.pin1
  VCC: U1.VCC, U3.VCC, Power_plug1.VCC
  GND_3: U1.GND, U3.GND, Power_plug1.GND, F1.1
  N20: U1.IN1, U1.IN2, U3.IN1, U3.IN2, S1.leg0
  N21: U1.K1-In, M1.pin_1
  N22: U1.K1-Off, U3.K1-Off
  N23: U1.K2-In, M1.pin_2
  N24: U1.K2-Off, U3.K2-Off
  N25: U2.K1-In, U2.K2-In
  N26: U2.K1-On, M3.C
  N27: U2.K2-On, M3.D
  N28: U3.K1-In, M2.pin_1
  N29: U3.K2-In, M2.pin_2
  N30: U4.P, F1.2
  N31: M3.A, M3.B
  N32: Part2.D3, J1.pin2
  N33: S5.leg0, S6.leg0, S7.leg1

notes:
  Switch BOX per controllo Batterie
  (collegato a NC dei rele)
  Driver DC
  dir1 - D5
  pwm1 - D4
  dir2 - D6
  pwm - D7
  Sistema di sicurezza
  inclinazione
  Interrutore a chiave per passare a batteria
  Switch NC in serie come sicurezza stop motori inclinazione
  12 Vcc
  Fusibile (500 mA) per evitare che un corto circuito nella linea dei pulsanti possa fare danni
  24 Vcc
  Pistoni SX
  Pistoni DX
  usando TSOP 38xx Collegamenti come da immagine
  Driver Stepper
  CLK+ pin 24
  CLK- pin GND
  CW+ pin 22
  CW- pin GND
  EN+ pin 30
  EN- pin 28
  Rele per salvaguardare il driver durante la rotazione manuale
  B - bianco
  B + verde
  A - giallo
  A+ marrone
  Allarme temperatura con sonde digitali ad alta precisione DS18B20
  driver stepper
  driver DC SX
  driver DC DX
  Step Down
  R1-4 1K
  UP
  DOWN
  SX
  DX
  Consenso inclinazione

custom parts:
  : Multichannel Optocoupler with Phototransistor Output
  MPU-6050 Board GY-521: Acelerometro y Giroscopio MPU-6050 Board GY-521
  Round Pushbutton: A generic pushbutton NC
  2-Channel 5v Relay Shield: 2 Channel 5v Relay Shield w. 2x SPD-06VDC-SD-C
